# Fritzing sketch Terrariumsteuerung (saved by Fritzing 1.0.6)

parts:
  M1 = BME280
  F1 = Fan - 4 wire [package=THT]
  F2 = Fan - 4 wire [package=THT]
  J1 = Power Jack [package=power_jack_slot]
  J2 = Power Plug
  Mod1 = KY-019 5V Relay Module [package="Breakout board"]
  Mod2 = KY-019 5V Relay Module [package="Breakout board"]
  J3 = 220v plug
  Pumpe_Beregnungsanlage = Solenoid
  ESP32-C1 = esp32-c3-supermini-with-display

nets:
  VIN: M1.VIN, ESP32-C1.3v3
  GND: M1.GND, F1.GND, F2.GND, J1.GND, J2.GND, Mod1.-, Mod2.-, ESP32-C1.gnd
  N1: M1.SCL, ESP32-C1.gpio6
  N2: M1.SDA, ESP32-C1.gpio5
  N3: F1.Power, F2.Power, Mod2.NO
  N4: F1.PWM, F2.PWM, ESP32-C1.gpio3
  N5: F2.Tach, ESP32-C1.gpio4
  N6: J1.PWR, J1.tip_PWR, J2.PWR, Mod2.Common
  N7: Mod1.S, ESP32-C1.gpio1
  N8: Mod1.+, Mod2.+, ESP32-C1.5v
  N9: Mod1.Common, Pumpe_Beregnungsanlage.pin1
  N10: Mod1.NO, J3.pin1
  N11: Mod2.S, ESP32-C1.gpio2
  N12: J3.pin2, Pumpe_Beregnungsanlage.pin2

custom parts:
  BME280: Temperature Humidity Barometric presure Sensor
  Fan - 4 wire: Fan, 4 wire with tach.
  Power Jack: Power Jack This is the standard 5.5mm barrel jack for power. Ths one is modified to mate with the barrel plug part and allow the two to "connect" so batteries and wall warts can be "connected" in breadboard and will go through to schematic.
  Power Plug: Power Jack This is the standard 5.5mm barrel plug for power. This part has bendable leads (i.e. wires in the real world) to connect to wall warts or the breadboard in the standard wire end, and hidden connectors on the tip end that will connect when "plugged in" (overlapped with the jack so it appears "plugged in" in breadboard) to the modified coax jack part. Internal busses connect the two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
  KY-019 5V Relay Module: KY-019 5V Relay module, used to control AC circuits. (Special thanks to vanepp for fixing the PCB holes and other errors)
  220v plug: Generic 220V AC plug.
